// Logisim project z80.circ as structural Verilog: 16 circuits, main circuit test
module test (
  input  [7:0] in_1,
  input  [7:0] in_2,
  input  in_3,
  input  in_4,
  input  in_5,
  input  in_6,
  input  [7:0] in_7,
  input  [7:0] in_8,
  output [6:0] out_9
);

  wire button_1_out, button_2_out, button_3_out, button_4_out, clear_out, enter_out, undriven;
  wire [7:0] counter_1_q, register_2_q, subtractor_1_out, undriven_2;
  wire [15:0] rom_2_data;
  wire [31:0] rom_1_data;

  IDynamicMemories_F23 idynamicmemories_f23_1 ();  // open: neg_RFSH, neg_MREQ, A12, A11_A0, D7_D0, neg_WR
  Button button_1 (.out(button_1_out));
  Register register_1 (
    .D({in_4, in_3, in_6, {2{in_5}}, in_6, in_4, in_3}), .en(button_1_out), .clk(button_1_out));  // open: Q, clr
  ROM #(.dataWidth(32)) rom_1 (.addr(in_8), .data(rom_1_data));
  Button button_2 (.out(button_2_out));
  Register register_2 (.D(in_1), .en(button_2_out), .clk(button_2_out), .Q(register_2_q));  // open: clr
  // Probe on rom_1_data
  // Probe on register_2_q
  Decoder decoder_1 ();  // open: out0, out1, sel, en
  Button button_3 (.out(button_3_out));
  Button button_4 (.out(button_4_out));
  Counter counter_1 (
    .clr(button_3_out), .up(1'b1), .clk(button_4_out), .Q(counter_1_q));  // open: load, count, D, carry
  ROM #(.dataWidth(16)) rom_2 (.addr(counter_1_q), .data(rom_2_data));
  Button enter (.out(enter_out));
  Keyboard #(.buflen(1)) keyboard_1 (.clk(enter_out), .re(undriven), .clr(clear_out));  // open: avail, data
  Button clear (.out(clear_out));
  Subtractor subtractor_1 (.a(undriven_2), .b(8'h48), .out(subtractor_1_out));  // open: bin, bout
  Decoder decoder_2 ();  // open: out0, out1, sel, en

  // Notes on the sheet:
  //   contents of rom_1 (hex, n*v repeats v):
  //   432423 1 0 0 0 222 3 6*0 445 4*0 32214 0 0 0 41242145 22*0 5
  //   op code = 10 bitow na instrukcje, 6 bitow na rejestry
  //   0-2 -> src, 3-5 -> dst
  //   contents of rom_2 (hex, n*v repeats v):
  //   0 11
  //   jesli operacja rejestrowa
  //   jesli immediate
  //   n
  //   op code
  //   op code = 8 bitow na instr, 8 dla n
endmodule

module IDynamicMemories_F23 (
  input  neg_RFSH,
  input  neg_MREQ,
  input  A12,
  input  [11:0] A11_A0,
  input  [7:0] D7_D0,
  input  neg_WR
);

  wire and_1_out, and_2_out, and_3_out, button_1_out, clk, or_1_out, or_2_out, Read, Write;
  wire [7:0] controlled_buffer_2_out, controlled_buffer_3_out;

  Clock clock_1 (.out(clk));
  Button button_1 (.out(button_1_out));
  Controlled_Buffer controlled_buffer_1 ();  // open: in, out, en
  Controlled_Inverter controlled_inverter_1 ();  // open: in, out, en
  assign controlled_buffer_2_out = Write ? D7_D0 : 8'bz;  // Controlled_Buffer controlled_buffer_2
  assign controlled_buffer_3_out = Read ? controlled_buffer_2_out : 8'bz;  // Controlled_Buffer controlled_buffer_3
  // Probe on controlled_buffer_3_out
  D_Flip_Flop d_ff_1 (.D(neg_WR), .clk(clk), .Q(Write), .Qn(Read));  // open: preset, reset
  not not_1 (neg_MREQ, A12);
  and and_1 (and_1_out, ~neg_RFSH, ~neg_MREQ);  // AND_Gate
  and and_2 (and_2_out, ~neg_MREQ, ~A12);  // AND_Gate
  and and_3 (and_3_out, ~neg_MREQ, ~neg_MREQ);  // AND_Gate
  or or_1 (or_1_out, and_1_out, and_2_out);
  or or_2 (or_2_out, and_1_out, and_3_out);
  RAM #(.addrWidth(12), .clearpin("true"), .databus("bidir")) ram_1 (
    .addr(A11_A0), .we(Write), .oe(Read), .clk(clk), .data(controlled_buffer_2_out), .clr(or_2_out));
  RAM #(.addrWidth(12), .clearpin("true"), .databus("bidir")) ram_2 (
    .addr(A11_A0), .we(Write), .oe(Read), .clk(clk), .data(controlled_buffer_2_out), .clr(or_1_out));
endmodule

module WaitStateM1 (
  input  negM1,
  output negWAIT
);

  wire CLK_out, d_ff_2_q, not_1_out, not_2_out, not_3_out, not_4_out;

  Clock CLK (.out(CLK_out));
  not not_1 (not_1_out, d_ff_2_q);
  D_Flip_Flop d_ff_1 (.D(negM1), .clk(CLK_out), .Q(negWAIT), .preset(not_1_out), .reset(not_2_out));  // open: Qn
  not not_2 (not_2_out, 1'b1);
  not not_3 (not_3_out, 1'b1);
  D_Flip_Flop d_ff_2 (.D(negWAIT), .clk(CLK_out), .Q(d_ff_2_q), .preset(not_3_out), .reset(not_4_out));  // open: Qn
  not not_4 (not_4_out, 1'b1);
endmodule

module WaitStateAnyMemory (
  input  negMREQ,
  output negWAIT
);

  wire CLK_out, d_ff_1_q, d_ff_1_qn, d_ff_2_q, not_1_out, not_2_out, not_3_out, not_4_out;

  Clock CLK (.out(CLK_out));
  not not_1 (not_1_out, 1'b1);
  D_Flip_Flop d_ff_1 (.D(negMREQ), .clk(CLK_out), .Q(d_ff_1_q), .Qn(d_ff_1_qn), .preset(not_1_out), .reset(not_2_out));
  not not_2 (not_2_out, 1'b1);
  not not_3 (not_3_out, d_ff_1_qn);
  D_Flip_Flop d_ff_2 (.D(d_ff_1_q), .clk(CLK_out), .Q(d_ff_2_q), .preset(not_3_out), .reset(not_4_out));  // open: Qn
  not not_4 (not_4_out, 1'b1);
  nand nand_1 (negWAIT, d_ff_1_qn, d_ff_2_q);
endmodule

module inc_8bit (
  input  [7:0] reg_in,
  output [7:0] inc_out,
  output flag_z,
  output flag_s,
  output flag_h,
  output flag_n,
  output flag_pv
);

  wire [7:1] undriven;

  Comparator comparator_1 (.a(reg_in), .b(8'h7f), .eq(flag_pv));  // open: gt, lt
  add_8bit add_8bit_1 (
    .Acc_in({undriven, 1'b1}), .reg_in(reg_in), .acc_out(inc_out), .flag_z(flag_z), .flag_s(flag_s),
    .flag_h(flag_h));  // open: flag_c, flag_pv, flag_n

  assign flag_n = 1'b0;

  // Notes on the sheet:
  //   N is reset. C is not affected
  //   H is set if carry from bit 3; otherwise, it is reset. P/V is set if r was 7Fh before operation; otherwise, it is reset
  //   S is set if result is negative; otherwise, it is reset. Z is set if result is 0; otherwise, it is reset. 
endmodule

module add_8bit (
  input  [7:0] Acc_in,
  input  [7:0] reg_in,
  output [7:0] acc_out,
  output flag_z,
  output flag_s,
  output flag_h,
  output flag_c,
  output flag_pv,
  output flag_n
);

  wire adder_2_cout;

  Adder #(.width(4)) adder_1 (.a(reg_in[3:0]), .b(Acc_in[3:0]), .cout(flag_h));  // open: out, cin
  Adder #(.width(7)) adder_2 (.a(Acc_in[6:0]), .b(reg_in[6:0]), .cout(adder_2_cout));  // open: out, cin
  Adder adder_3 (.a(reg_in), .b(Acc_in), .out(acc_out), .cout(flag_c));  // open: cin
  Comparator comparator_1 (.a(acc_out), .b({8{1'b0}}), .eq(flag_z), .lt(flag_s));  // open: gt
  xor xor_1 (flag_pv, flag_c, adder_2_cout);

  assign flag_n = 1'b0;

  // Other names for the same wires on the sheet: Acc[7:0] = Acc_in

  // Notes on the sheet:
  //   P/V is set if overflow; otherwise, it is reset. N is reset. C is set if carry from bit 7; otherwise, it is reset.
  //   S is set if result is negative; otherwise, it is reset. Z is set if result is 0; otherwise, it is reset. H is set if carry from bit 3; otherwise, it is reset.
endmodule

module main (
  input  inc_or_dec,
  output [7:0] out_2,
  output [7:0] out_3
);

  wire A_alu_enable, A_enable, and_1_out, and_2_out, and_4_out, and_6_out, and_10_out, and_11_out,
       and_12_out, and_13_out, and_14_out, and_15_out, and_16_out, and_17_out, and_18_out, and_19_out,
       B_enable, button_2_out, C_enable, carry, clk, D_enable, decoder_3_out1, E_enable, flag_c, flag_c_out,
       flag_h, flag_h_out, flag_n, flag_n_out, flag_pv, flag_pv_out, flag_s, flag_s_out, flag_z, flag_z_out,
       H_enable, hl_enable, imm_decd, instr24, jp_cc, jp_cc_nn, jp_nn, L_enable, LD_dd_nn, ld_enable, load,
       load_hl_r, load_imm, load_r_hl, nand_1_out, no_carry, non_zero, nor_1_out, nor_2_out, nor_3_out,
       nor_4_out, not_1_out, not_2_out, not_3_out, not_4_out, not_5_out, not_6_out, not_7_out, not_8_out,
       not_9_out, or_1_out, or_2_out, or_4_out, or_5_out, or_6_out, or_7_out, or_9_out, or_10_out, or_11_out,
       parity_even, parity_odd, reg_decd, sign_negative, sign_positive, zero;
  wire [2:0] controlled_buffer_4_out, reg_bits;
  wire [7:0] A_q, B_q, C_q, controlled_buffer_8_out, controlled_buffer_9_out, controlled_buffer_14_out, D_q,
       demultiplexer_1_out0, demultiplexer_1_out1, demultiplexer_1_out2, demultiplexer_1_out3,
       demultiplexer_1_out4, demultiplexer_1_out5, demultiplexer_1_out7, E_q, multiplexer_1_out,
       multiplexer_2_out, ram_1_dout, ram_data;
  wire [15:0] counter_1_q, L_q;
  wire [23:0] instr;

  Clock clock_1 (.out(clk));
  Button button_1 ();  // open: out
  or or_1 (or_1_out, jp_cc_nn, jp_nn);
  Button button_2 (.out(button_2_out));
  Decoder #(.select(2)) decoder_1 (.out2(hl_enable), .sel(instr[21:20]), .en(LD_dd_nn));  // open: out0, out1, out3
  nand nand_1 (nand_1_out, instr[0], instr[7]);
  Counter #(.max('hffff), .width(16)) counter_1 (
    .clr(button_2_out), .load(or_1_out), .up(inc_or_dec), .clk(clk), .D(instr[15:0]), .Q(counter_1_q));  // open: count, carry
  Decoder #(.select(3)) decoder_2 (
    .out6(load_imm), .sel(instr[10:8]), .en(imm_decd));  // open: out0, out1, out2, out3, out4, out5, out7
  nor nor_1 (nor_1_out, instr[17], instr[18], instr[19], instr[22], instr[23]);
  and and_1 (and_1_out, instr[1], instr[2], instr[6]);
  and and_2 (and_2_out, instr[16], nor_1_out);
  and and_3 (load_r_hl, nand_1_out, and_1_out);
  nor nor_2 (nor_2_out, instr[3], instr[7]);
  and and_4 (and_4_out, instr[4], instr[5], instr[6]);
  and and_5 (LD_dd_nn, and_2_out, instr24);
  and and_6 (and_6_out, nor_2_out, and_4_out);
  ROM #(.addrWidth(16), .dataWidth(24)) rom_1 (.addr(counter_1_q), .data(instr));
  Decoder #(.select(2)) decoder_3 (.out1(decoder_3_out1), .sel(instr[7:6]), .en(reg_decd));  // open: out0, out2, out3
  and and_7 (load_hl_r, and_6_out, reg_decd);
  or or_2 (or_2_out, instr[8], instr[9], instr[10], instr[11], instr[12], instr[13], instr[14], instr[15]);
  or or_3 (instr24, instr[16], instr[17], instr[18], instr[19], instr[20], instr[21], instr[22], instr[23]);
  not not_1 (not_1_out, load_hl_r);
  not not_2 (not_2_out, load_r_hl);
  not not_3 (not_3_out, instr24);
  Decoder #(.select(3)) decoder_4 (
    .out0(non_zero), .out1(zero), .out2(no_carry), .out3(carry), .out4(parity_odd), .out5(parity_even),
    .out6(sign_positive), .out7(sign_negative), .sel(instr[21:19]), .en(jp_cc));
  and and_8 (load, not_1_out, not_2_out, decoder_3_out1);
  and and_9 (imm_decd, or_2_out, not_3_out);
  nor nor_3 (nor_3_out, instr[18], instr[19], instr[20], instr[21]);
  and and_10 (and_10_out, instr[17], instr[22], instr[23]);
  not not_4 (not_4_out, flag_z_out);
  not not_5 (not_5_out, flag_c_out);
  not not_6 (not_6_out, flag_pv_out);
  not not_7 (not_7_out, flag_s_out);
  and and_11 (and_11_out, sign_positive, sign_negative);
  and and_12 (and_12_out, instr[16], instr[17], instr[22], instr[23]);
  nor nor_4 (nor_4_out, instr[16], instr[18]);
  and and_13 (and_13_out, non_zero, not_4_out);
  and and_14 (and_14_out, zero, flag_z_out);
  and and_15 (and_15_out, no_carry, not_5_out);
  and and_16 (and_16_out, carry, flag_c_out);
  and and_17 (and_17_out, parity_odd, not_6_out);
  and and_18 (and_18_out, parity_even, flag_pv_out);
  and and_19 (and_19_out, sign_positive, not_7_out);
  assign reg_bits = load_r_hl ? instr[5:3] : 3'bz;  // Controlled_Buffer controlled_buffer_1
  assign reg_bits = not_8_out ? instr[2:0] : 3'bz;  // Controlled_Buffer controlled_buffer_2
  and and_20 (jp_nn, and_12_out, nor_3_out);
  and and_21 (jp_cc, and_10_out, nor_4_out);
  not not_8 (not_8_out, load_r_hl);
  assign ram_data = load_imm ? instr[7:0] : 8'bz;  // Controlled_Buffer controlled_buffer_3
  Decoder #(.select(3)) decoder_5 (
    .out0(B_enable), .out1(C_enable), .out2(D_enable), .out3(E_enable), .out4(H_enable), .out5(L_enable),
    .out7(A_enable), .sel(controlled_buffer_4_out), .en(or_4_out));  // open: out6
  or or_4 (or_4_out, load, load_r_hl, load_imm);
  assign controlled_buffer_4_out = or_7_out ? reg_bits : 3'bz;  // Controlled_Buffer controlled_buffer_4
  or or_5 (or_5_out, and_13_out, and_14_out, and_15_out, and_16_out, and_17_out, and_18_out, and_19_out, and_11_out);
  assign ram_data = load ? multiplexer_1_out : 8'bz;  // Controlled_Buffer controlled_buffer_5
  assign controlled_buffer_4_out = load ? instr[5:3] : 3'bz;  // Controlled_Buffer controlled_buffer_6
  or or_6 (or_6_out, instr[0], instr[1], instr[2], instr[3], instr[4], instr[5], instr[6], instr[7]);
  not not_9 (not_9_out, imm_decd);
  and and_22 (jp_cc_nn, or_5_out, jp_cc);
  Demultiplexer #(.enable("true"), .select(3), .width(8)) demultiplexer_1 (
    .out0(demultiplexer_1_out0), .out1(demultiplexer_1_out1), .out2(demultiplexer_1_out2),
    .out3(demultiplexer_1_out3), .out4(demultiplexer_1_out4), .out5(demultiplexer_1_out5),
    .out7(demultiplexer_1_out7), .in(ram_data), .sel(controlled_buffer_4_out), .en(or_4_out));  // open: out6
  assign controlled_buffer_4_out = load_imm ? instr[13:11] : 3'bz;  // Controlled_Buffer controlled_buffer_7
  or or_7 (or_7_out, load_hl_r, load_r_hl);
  and and_23 (reg_decd, or_6_out, not_9_out);
  assign controlled_buffer_8_out = ld_enable ? demultiplexer_1_out4 : 8'bz;  // Controlled_Buffer controlled_buffer_8
  assign controlled_buffer_9_out = ld_enable ? demultiplexer_1_out5 : 8'bz;  // Controlled_Buffer controlled_buffer_9
  or or_8 (ld_enable, load, load_imm);
  assign controlled_buffer_9_out = hl_enable ? instr[7:0] : 8'bz;  // Controlled_Buffer controlled_buffer_10
  Register L (.D(controlled_buffer_9_out), .en(or_9_out), .clk(clk), .Q(L_q[7:0]));  // open: clr
  or or_9 (or_9_out, L_enable, hl_enable);
  assign out_3 = ld_enable ? demultiplexer_1_out7 : 8'bz;  // Controlled_Buffer controlled_buffer_11
  assign controlled_buffer_8_out = hl_enable ? instr[15:8] : 8'bz;  // Controlled_Buffer controlled_buffer_12
  Register H (.D(controlled_buffer_8_out), .en(or_10_out), .clk(clk), .Q(L_q[15:8]));  // open: clr
  or or_10 (or_10_out, H_enable, hl_enable);
  or or_11 (or_11_out, A_alu_enable, A_enable);
  Register E (.D(demultiplexer_1_out3), .en(E_enable), .clk(clk), .Q(E_q));  // open: clr
  Register C (.D(demultiplexer_1_out1), .en(C_enable), .clk(clk), .Q(C_q));  // open: clr
  Register D (.D(demultiplexer_1_out2), .en(D_enable), .clk(clk), .Q(D_q));  // open: clr
  Register A (.D(out_3), .en(or_11_out), .clk(clk), .Q(A_q));  // open: clr
  Register B (.D(demultiplexer_1_out0), .en(B_enable), .clk(clk), .Q(B_q));  // open: clr
  Multiplexer #(.select(3), .width(8)) multiplexer_1 (
    .in0(B_q), .in1(C_q), .in2(D_q), .in3(E_q), .in4(L_q[15:8]), .in5(L_q[7:0]), .out(multiplexer_1_out),
    .sel(reg_bits));  // open: in6, in7
  FLAG_REG flag_reg_1 (
    .flag_C_in(flag_c), .flag_N_in(flag_n), .flag_PV_in(flag_pv), .flag_H_in(flag_h), .flag_Z_in(flag_z),
    .flag_S_in(flag_s), .clock(clk), .flag_C_out(flag_c_out), .flag_N_out(flag_n_out),
    .flag_PV_out(flag_pv_out), .flag_H_out(flag_h_out), .flag_Z_out(flag_z_out), .flag_S_out(flag_s_out));  // open: alu_enable, out_9
  RAM #(.addrWidth(16), .enables("line")) ram_1 (
    .addr(L_q), .we(load_hl_r), .clk(clk), .din(controlled_buffer_14_out), .dout(ram_1_dout));
  assign ram_data = load_r_hl ? ram_1_dout : 8'bz;  // Controlled_Buffer controlled_buffer_13
  Multiplexer #(.select(3), .width(8)) multiplexer_2 (
    .in0(B_q), .in1(C_q), .in2(D_q), .in3(E_q), .in4(L_q[15:8]), .in5(L_q[7:0]), .in7(A_q),
    .out(multiplexer_2_out), .sel(reg_bits));  // open: in6
  assign controlled_buffer_14_out = load_hl_r ? multiplexer_2_out : 8'bz;  // Controlled_Buffer controlled_buffer_14
  assign out_2 = reg_decd ? multiplexer_2_out : 8'bz;  // Controlled_Buffer controlled_buffer_15
  assign out_2 = imm_decd ? instr[7:0] : 8'bz;  // Controlled_Buffer controlled_buffer_16
  ALU alu_1 (
    .acc_in(A_q), .arg(out_2), .flag_pv_in(flag_pv_out), .flag_n_in(flag_n_out), .flag_h_in(flag_h_out),
    .flag_s_in(flag_s_out), .flag_z_in(flag_z_out), .flag_c_in(flag_c_out), .op_code(instr), .acc_out(out_3),
    .flag_pv_out(flag_pv), .flag_n_out(flag_n), .flag_h_out(flag_h), .flag_s_out(flag_s),
    .flag_z_out(flag_z), .flag_c_out(flag_c), .alu_operation(A_alu_enable));  // open: temp, flags_operation

  // Other names for the same wires on the sheet: nn[15:0] = instr[15:0]; n[7:0] = instr[7:0]; ram_write = load_hl_r

  // Notes on the sheet:
  //   inc_or_dec: initial=0x1
  //   nn
  //   op code
  //   contents of rom_1 (hex, n*v repeats v):
  //   0 628 50 80 b8 210032 72 5e 2f ca0000 37 3f c30000
  //   jesli operacja rejestrowa
  //   dst_decoder
  //   001 Zero (Z) Z
  //   010 No Carry (NC) C
  //   011 Carry (C) C
  //   000 Non-Zero (NZ) Z
  //   100 Parity Odd (PO) P/V
  //   101 Parity Even (PE) P/V
  //   110 Sign Positive (P) S
  //   111 Sign Negative (M) S 
  //   przy kazdym loadzie inne rejestry sie resetuja, potrzebny bedzie jakis bufor?
  //   src_mux
endmodule

module load_r_r (
  input  [7:0] B_in,
  input  [7:0] C_in,
  input  [7:0] D_in,
  input  [7:0] E_in,
  input  [7:0] H_in,
  input  [7:0] L_in,
  input  [7:0] A_in,
  input  [2:0] reg_from,
  input  [2:0] reg_to,
  output [7:0] B_out,
  output [7:0] C_out,
  output [7:0] D_out,
  output [7:0] E_out,
  output [7:0] H_out,
  output [7:0] L_out,
  output [7:0] A_out
);

  wire [7:0] multiplexer_1_out;

  Multiplexer #(.select(3), .width(8)) multiplexer_1 (
    .in0(B_in), .in1(C_in), .in2(D_in), .in3(E_in), .in4(H_in), .in5(L_in), .in7(A_in),
    .out(multiplexer_1_out), .sel(reg_from));  // open: in6
  Demultiplexer #(.select(3), .width(8)) demultiplexer_1 (
    .out0(B_out), .out1(C_out), .out2(D_out), .out3(E_out), .out4(H_out), .out5(L_out), .out7(A_out),
    .in(multiplexer_1_out), .sel(reg_to));  // open: out6

  // Notes on the sheet:
  //   110 by default?
endmodule

module load_r_n (
  input  [7:0] n,
  input  [2:0] reg_to,
  output [7:0] B_out,
  output [7:0] C_out,
  output [7:0] D_out,
  output [7:0] E_out,
  output [7:0] H_out,
  output [7:0] L_out,
  output [7:0] A_out
);

  Demultiplexer #(.select(3), .width(8)) demultiplexer_1 (
    .out0(B_out), .out1(C_out), .out2(D_out), .out3(E_out), .out4(H_out), .out5(L_out), .out7(A_out), .in(n),
    .sel(reg_to));  // open: out6
endmodule

module ALU (
  input  [7:0] acc_in,
  input  [7:0] arg,
  input  flag_pv_in,
  input  flag_n_in,
  input  flag_h_in,
  input  flag_s_in,
  input  flag_z_in,
  input  flag_c_in,
  input  temp,
  input  [23:0] op_code,
  output [7:0] acc_out,
  output flag_pv_out,
  output flag_n_out,
  output flag_h_out,
  output flag_s_out,
  output flag_z_out,
  output flag_c_out,
  output alu_operation,
  output flags_operation
);

  wire adc, adc_8bit_1_flag_c_out, adc_8bit_1_flag_h, adc_8bit_1_flag_n, adc_8bit_1_flag_pv,
       adc_8bit_1_flag_s, adc_8bit_1_flag_z, add, add_8bit_1_flag_c, add_8bit_1_flag_h, add_8bit_1_flag_n,
       add_8bit_1_flag_pv, add_8bit_1_flag_s, add_8bit_1_flag_z, and_2_out, and_3_out, and_4_out, and_5_out,
       and_6_out, and_7_out, and_8_out, and_10_out, and_11_out, and_12_out, and_13_out, and_15_out,
       and_16_out, and_22_out, and_23_out, and_25_out, and_26_out, and_27_out, and_28_out, and_29_out,
       and_30_out, and_31_out, and_32_out, and_33_out, and_34_out, and_35_out, and_36_out, and_37_out,
       and_38_out, and_39_out, and_40_out, and_41_out, and_42_out, and_43_out, and_44_out, and_45_out,
       and_46_out, and_47_out, and_48_out, ANDl, ccf, cp, cp_8bit_1_flag_c, cp_8bit_1_flag_h,
       cp_8bit_1_flag_n, cp_8bit_1_flag_pv, cp_8bit_1_flag_s, cp_8bit_1_flag_z, cpl, inc_8bit_1_flag_h,
       inc_8bit_1_flag_n, inc_8bit_1_flag_pv, inc_8bit_1_flag_s, inc_8bit_1_flag_z, instr8, instr16,
       nand_1_out, neg, neg_8bit_1_flag_c_out, neg_8bit_1_flag_h, neg_8bit_1_flag_n, neg_8bit_1_flag_pv,
       neg_8bit_1_flag_s, neg_8bit_1_flag_z, nor_1_out, nor_2_out, nor_3_out, nor_4_out, nor_5_out,
       nor_6_out, nor_7_out, nor_8_out, nor_9_out, nor_10_out, nor_11_out, nor_12_out, nor_13_out,
       nor_14_out, nor_15_out, nor_16_out, nor_17_out, nor_18_out, nor_19_out, nor_20_out, nor_21_out,
       not_1_out, not_2_out, not_3_out, not_4_out, not_5_out, not_6_out, not_7_out, not_8_out, not_9_out,
       not_10_out, not_11_out, not_12_out, not_14_out, not_15_out, not_16_out, ORl, rla, rlca, rra, rrca,
       sbc, sbc_8bit_1_flag_c_out, sbc_8bit_1_flag_h, sbc_8bit_1_flag_n, sbc_8bit_1_flag_pv,
       sbc_8bit_1_flag_s, sbc_8bit_1_flag_z, scf, sub, sub_8bit_1_flag_c, sub_8bit_1_flag_h,
       sub_8bit_1_flag_n, sub_8bit_1_flag_pv, sub_8bit_1_flag_s, sub_8bit_1_flag_z, XORl;
  wire [7:0] adc_8bit_1_acc_out, add_8bit_1_acc_out, and_1_out, controlled_buffer_1_out,
       controlled_buffer_2_out, controlled_buffer_3_out, controlled_buffer_4_out, controlled_buffer_5_out,
       controlled_buffer_6_out, controlled_buffer_7_out, controlled_buffer_8_out, controlled_buffer_9_out,
       controlled_buffer_10_out, controlled_buffer_11_out, controlled_buffer_12_out,
       controlled_buffer_13_out, controlled_buffer_14_out, controlled_buffer_15_out,
       controlled_buffer_23_out, controlled_buffer_64_out, controlled_buffer_68_out,
       controlled_buffer_69_out, controlled_buffer_71_out, controlled_buffer_72_out,
       controlled_buffer_73_out, inc_8bit_1_inc_out, neg_8bit_1_acc_out, or_1_out, sbc_8bit_1_acc_out,
       sub_8bit_1_reg_a_out, xor_1_out;

  assign controlled_buffer_1_out = adc ? acc_in : 8'bz;  // Controlled_Buffer controlled_buffer_1
  assign controlled_buffer_2_out = adc ? arg : 8'bz;  // Controlled_Buffer controlled_buffer_2
  assign controlled_buffer_3_out = cp ? acc_in : 8'bz;  // Controlled_Buffer controlled_buffer_3
  assign controlled_buffer_4_out = add ? acc_in : 8'bz;  // Controlled_Buffer controlled_buffer_4
  assign controlled_buffer_5_out = add ? arg : 8'bz;  // Controlled_Buffer controlled_buffer_5
  assign controlled_buffer_6_out = sbc ? acc_in : 8'bz;  // Controlled_Buffer controlled_buffer_6
  assign controlled_buffer_7_out = sbc ? arg : 8'bz;  // Controlled_Buffer controlled_buffer_7
  assign controlled_buffer_8_out = sub ? acc_in : 8'bz;  // Controlled_Buffer controlled_buffer_8
  assign controlled_buffer_9_out = sub ? arg : 8'bz;  // Controlled_Buffer controlled_buffer_9
  assign controlled_buffer_10_out = cp ? arg : 8'bz;  // Controlled_Buffer controlled_buffer_10
  assign controlled_buffer_11_out = neg ? acc_in : 8'bz;  // Controlled_Buffer controlled_buffer_11
  assign controlled_buffer_12_out = rrca ? acc_in : 8'bz;  // Controlled_Buffer controlled_buffer_12
  assign controlled_buffer_13_out = ANDl ? acc_in : 8'bz;  // Controlled_Buffer controlled_buffer_13
  assign controlled_buffer_14_out = ANDl ? arg : 8'bz;  // Controlled_Buffer controlled_buffer_14
  add_8bit add_8bit_1 (
    .Acc_in(controlled_buffer_4_out), .reg_in(controlled_buffer_5_out), .acc_out(add_8bit_1_acc_out),
    .flag_z(add_8bit_1_flag_z), .flag_s(add_8bit_1_flag_s), .flag_h(add_8bit_1_flag_h),
    .flag_c(add_8bit_1_flag_c), .flag_pv(add_8bit_1_flag_pv), .flag_n(add_8bit_1_flag_n));
  sub_8bit sub_8bit_1 (
    .reg_A_in(controlled_buffer_8_out), .op_1(controlled_buffer_9_out), .reg_a_out(sub_8bit_1_reg_a_out),
    .flag_z(sub_8bit_1_flag_z), .flag_s(sub_8bit_1_flag_s), .flag_h(sub_8bit_1_flag_h),
    .flag_c(sub_8bit_1_flag_c), .flag_pv(sub_8bit_1_flag_pv), .flag_n(sub_8bit_1_flag_n));
  adc_8bit adc_8bit_1 (
    .flag_c_in(flag_c_in), .acc_in(controlled_buffer_1_out), .reg_in(controlled_buffer_2_out),
    .acc_out(adc_8bit_1_acc_out), .flag_h(adc_8bit_1_flag_h), .flag_z(adc_8bit_1_flag_z),
    .flag_s(adc_8bit_1_flag_s), .flag_pv(adc_8bit_1_flag_pv), .flag_n(adc_8bit_1_flag_n),
    .flag_c_out(adc_8bit_1_flag_c_out));
  cp_8bit cp_8bit_1 (
    .reg_A_in(controlled_buffer_3_out), .op_1(controlled_buffer_10_out), .flag_z(cp_8bit_1_flag_z),
    .flag_s(cp_8bit_1_flag_s), .flag_h(cp_8bit_1_flag_h), .flag_c(cp_8bit_1_flag_c),
    .flag_pv(cp_8bit_1_flag_pv), .flag_n(cp_8bit_1_flag_n));
  assign and_1_out = controlled_buffer_13_out & controlled_buffer_14_out;  // AND_Gate and_1, 8 bits wide
  assign controlled_buffer_15_out = ORl ? acc_in : 8'bz;  // Controlled_Buffer controlled_buffer_15
  sbc_8bit sbc_8bit_1 (
    .flag_c_in(flag_c_in), .acc_in(controlled_buffer_6_out), .reg_in(controlled_buffer_7_out),
    .acc_out(sbc_8bit_1_acc_out), .flag_c_out(sbc_8bit_1_flag_c_out), .flag_z(sbc_8bit_1_flag_z),
    .flag_s(sbc_8bit_1_flag_s), .flag_n(sbc_8bit_1_flag_n), .flag_pv(sbc_8bit_1_flag_pv),
    .flag_h(sbc_8bit_1_flag_h));
  not not_1 (not_1_out, rrca);
  assign flag_h_out = rrca ? not_1_out : 1'bz;  // Controlled_Buffer controlled_buffer_16
  not not_2 (not_2_out, rrca);
  assign flag_n_out = rrca ? not_2_out : 1'bz;  // Controlled_Buffer controlled_buffer_17
  assign flag_c_out = rrca ? controlled_buffer_12_out[0] : 1'bz;  // Controlled_Buffer controlled_buffer_18
  assign flag_z_out = rrca ? flag_z_in : 1'bz;  // Controlled_Buffer controlled_buffer_19
  assign flag_pv_out = rrca ? flag_pv_in : 1'bz;  // Controlled_Buffer controlled_buffer_20
  assign flag_s_out = rrca ? flag_s_in : 1'bz;  // Controlled_Buffer controlled_buffer_21
  assign acc_out = ANDl ? and_1_out : 8'bz;  // Controlled_Buffer controlled_buffer_22
  assign controlled_buffer_23_out = ORl ? arg : 8'bz;  // Controlled_Buffer controlled_buffer_23
  neg_8bit neg_8bit_1 (
    .acc_in(controlled_buffer_11_out), .acc_out(neg_8bit_1_acc_out), .flag_z(neg_8bit_1_flag_z),
    .flag_c_out(neg_8bit_1_flag_c_out), .flag_s(neg_8bit_1_flag_s), .flag_h(neg_8bit_1_flag_h),
    .flag_n(neg_8bit_1_flag_n), .flag_pv(neg_8bit_1_flag_pv));
  assign flag_z_out = adc ? adc_8bit_1_flag_z : 1'bz;  // Controlled_Buffer controlled_buffer_24
  assign flag_pv_out = adc ? adc_8bit_1_flag_pv : 1'bz;  // Controlled_Buffer controlled_buffer_25
  assign flag_c_out = adc ? adc_8bit_1_flag_c_out : 1'bz;  // Controlled_Buffer controlled_buffer_26
  assign flag_pv_out = cp ? cp_8bit_1_flag_pv : 1'bz;  // Controlled_Buffer controlled_buffer_27
  assign or_1_out = controlled_buffer_15_out | controlled_buffer_23_out;  // OR_Gate or_1, 8 bits wide
  assign acc_out = ORl ? or_1_out : 8'bz;  // Controlled_Buffer controlled_buffer_28
  assign flag_z_out = add ? add_8bit_1_flag_z : 1'bz;  // Controlled_Buffer controlled_buffer_29
  assign flag_s_out = add ? add_8bit_1_flag_s : 1'bz;  // Controlled_Buffer controlled_buffer_30
  assign flag_h_out = add ? add_8bit_1_flag_h : 1'bz;  // Controlled_Buffer controlled_buffer_31
  assign flag_c_out = add ? add_8bit_1_flag_c : 1'bz;  // Controlled_Buffer controlled_buffer_32
  assign flag_pv_out = add ? add_8bit_1_flag_pv : 1'bz;  // Controlled_Buffer controlled_buffer_33
  assign flag_n_out = add ? add_8bit_1_flag_n : 1'bz;  // Controlled_Buffer controlled_buffer_34
  assign acc_out = sbc ? sbc_8bit_1_acc_out : 8'bz;  // Controlled_Buffer controlled_buffer_35
  assign flag_c_out = sbc ? sbc_8bit_1_flag_c_out : 1'bz;  // Controlled_Buffer controlled_buffer_36
  assign flag_z_out = sbc ? sbc_8bit_1_flag_z : 1'bz;  // Controlled_Buffer controlled_buffer_37
  assign flag_s_out = sbc ? sbc_8bit_1_flag_s : 1'bz;  // Controlled_Buffer controlled_buffer_38
  assign flag_n_out = sbc ? sbc_8bit_1_flag_n : 1'bz;  // Controlled_Buffer controlled_buffer_39
  assign flag_pv_out = sbc ? sbc_8bit_1_flag_pv : 1'bz;  // Controlled_Buffer controlled_buffer_40
  assign flag_h_out = sbc ? sbc_8bit_1_flag_h : 1'bz;  // Controlled_Buffer controlled_buffer_41
  assign acc_out = sub ? sub_8bit_1_reg_a_out : 8'bz;  // Controlled_Buffer controlled_buffer_42
  assign flag_z_out = sub ? sub_8bit_1_flag_z : 1'bz;  // Controlled_Buffer controlled_buffer_43
  assign flag_s_out = sub ? sub_8bit_1_flag_s : 1'bz;  // Controlled_Buffer controlled_buffer_44
  assign flag_h_out = sub ? sub_8bit_1_flag_h : 1'bz;  // Controlled_Buffer controlled_buffer_45
  assign flag_c_out = sub ? sub_8bit_1_flag_c : 1'bz;  // Controlled_Buffer controlled_buffer_46
  assign flag_pv_out = sub ? sub_8bit_1_flag_pv : 1'bz;  // Controlled_Buffer controlled_buffer_47
  assign flag_n_out = sub ? sub_8bit_1_flag_n : 1'bz;  // Controlled_Buffer controlled_buffer_48
  assign acc_out = adc ? adc_8bit_1_acc_out : 8'bz;  // Controlled_Buffer controlled_buffer_49
  assign flag_h_out = adc ? adc_8bit_1_flag_h : 1'bz;  // Controlled_Buffer controlled_buffer_50
  assign flag_s_out = adc ? adc_8bit_1_flag_s : 1'bz;  // Controlled_Buffer controlled_buffer_51
  assign flag_n_out = adc ? adc_8bit_1_flag_n : 1'bz;  // Controlled_Buffer controlled_buffer_52
  assign flag_z_out = cp ? cp_8bit_1_flag_z : 1'bz;  // Controlled_Buffer controlled_buffer_53
  assign flag_s_out = cp ? cp_8bit_1_flag_s : 1'bz;  // Controlled_Buffer controlled_buffer_54
  assign flag_h_out = cp ? cp_8bit_1_flag_h : 1'bz;  // Controlled_Buffer controlled_buffer_55
  assign flag_c_out = cp ? cp_8bit_1_flag_c : 1'bz;  // Controlled_Buffer controlled_buffer_56
  assign flag_n_out = cp ? cp_8bit_1_flag_n : 1'bz;  // Controlled_Buffer controlled_buffer_57
  assign acc_out = add ? add_8bit_1_acc_out : 8'bz;  // Controlled_Buffer controlled_buffer_58
  assign flag_z_out = neg ? neg_8bit_1_flag_z : 1'bz;  // Controlled_Buffer controlled_buffer_59
  assign flag_s_out = neg ? neg_8bit_1_flag_s : 1'bz;  // Controlled_Buffer controlled_buffer_60
  assign flag_n_out = neg ? neg_8bit_1_flag_n : 1'bz;  // Controlled_Buffer controlled_buffer_61
  assign flag_pv_out = neg ? neg_8bit_1_flag_pv : 1'bz;  // Controlled_Buffer controlled_buffer_62
  assign acc_out = rrca ? {controlled_buffer_12_out[0], controlled_buffer_12_out[7:1]} : 8'bz;  // Controlled_Buffer controlled_buffer_63
  assign controlled_buffer_64_out = XORl ? acc_in : 8'bz;  // Controlled_Buffer controlled_buffer_64
  assign acc_out = neg ? neg_8bit_1_acc_out : 8'bz;  // Controlled_Buffer controlled_buffer_65
  assign flag_c_out = neg ? neg_8bit_1_flag_c_out : 1'bz;  // Controlled_Buffer controlled_buffer_66
  assign flag_h_out = neg ? neg_8bit_1_flag_h : 1'bz;  // Controlled_Buffer controlled_buffer_67
  assign controlled_buffer_68_out = XORl ? arg : 8'bz;  // Controlled_Buffer controlled_buffer_68
  assign controlled_buffer_69_out = temp ? acc_in : 8'bz;  // Controlled_Buffer controlled_buffer_69
  assign xor_1_out = controlled_buffer_64_out ^ controlled_buffer_68_out;  // XOR_Gate xor_1, 8 bits wide
  assign acc_out = XORl ? xor_1_out : 8'bz;  // Controlled_Buffer controlled_buffer_70
  assign controlled_buffer_71_out = rlca ? acc_in : 8'bz;  // Controlled_Buffer controlled_buffer_71
  assign controlled_buffer_72_out = rra ? acc_in : 8'bz;  // Controlled_Buffer controlled_buffer_72
  not not_3 (not_3_out, scf);
  not not_4 (not_4_out, scf);
  assign controlled_buffer_73_out = rla ? acc_in : 8'bz;  // Controlled_Buffer controlled_buffer_73
  inc_8bit inc_8bit_1 (
    .reg_in(controlled_buffer_69_out), .inc_out(inc_8bit_1_inc_out), .flag_z(inc_8bit_1_flag_z),
    .flag_s(inc_8bit_1_flag_s), .flag_h(inc_8bit_1_flag_h), .flag_n(inc_8bit_1_flag_n),
    .flag_pv(inc_8bit_1_flag_pv));
  assign flag_h_out = scf ? not_3_out : 1'bz;  // Controlled_Buffer controlled_buffer_74
  assign flag_n_out = scf ? not_4_out : 1'bz;  // Controlled_Buffer controlled_buffer_75
  assign flag_c_out = scf ? scf : 1'bz;  // Controlled_Buffer controlled_buffer_76
  assign flag_z_out = scf ? flag_z_in : 1'bz;  // Controlled_Buffer controlled_buffer_77
  assign flag_pv_out = scf ? flag_pv_in : 1'bz;  // Controlled_Buffer controlled_buffer_78
  assign flag_s_out = scf ? flag_s_in : 1'bz;  // Controlled_Buffer controlled_buffer_79
  assign acc_out = cpl ? ~acc_in : 8'bz;  // Controlled_Inverter controlled_inverter_1
  not not_5 (not_5_out, rlca);
  not not_6 (not_6_out, rlca);
  not not_7 (not_7_out, rla);
  not not_8 (not_8_out, rla);
  not not_9 (not_9_out, rra);
  assign flag_h_out = rra ? not_9_out : 1'bz;  // Controlled_Buffer controlled_buffer_80
  not not_10 (not_10_out, rra);
  assign flag_n_out = rra ? not_10_out : 1'bz;  // Controlled_Buffer controlled_buffer_81
  assign flag_c_out = rra ? controlled_buffer_72_out[0] : 1'bz;  // Controlled_Buffer controlled_buffer_82
  assign flag_z_out = rra ? flag_z_in : 1'bz;  // Controlled_Buffer controlled_buffer_83
  assign flag_pv_out = rra ? flag_pv_in : 1'bz;  // Controlled_Buffer controlled_buffer_84
  assign flag_s_out = rra ? flag_s_in : 1'bz;  // Controlled_Buffer controlled_buffer_85
  assign flag_h_out = cpl ? cpl : 1'bz;  // Controlled_Buffer controlled_buffer_86
  assign flag_n_out = cpl ? cpl : 1'bz;  // Controlled_Buffer controlled_buffer_87
  assign flag_c_out = cpl ? flag_c_in : 1'bz;  // Controlled_Buffer controlled_buffer_88
  assign flag_z_out = cpl ? flag_z_in : 1'bz;  // Controlled_Buffer controlled_buffer_89
  assign flag_pv_out = cpl ? flag_pv_in : 1'bz;  // Controlled_Buffer controlled_buffer_90
  assign flag_s_out = cpl ? flag_s_in : 1'bz;  // Controlled_Buffer controlled_buffer_91
  assign flag_h_out = rlca ? not_5_out : 1'bz;  // Controlled_Buffer controlled_buffer_92
  assign flag_n_out = rlca ? not_6_out : 1'bz;  // Controlled_Buffer controlled_buffer_93
  assign flag_c_out = rlca ? controlled_buffer_71_out[7] : 1'bz;  // Controlled_Buffer controlled_buffer_94
  assign flag_z_out = rlca ? flag_z_in : 1'bz;  // Controlled_Buffer controlled_buffer_95
  assign flag_pv_out = rlca ? flag_pv_in : 1'bz;  // Controlled_Buffer controlled_buffer_96
  assign flag_s_out = rlca ? flag_s_in : 1'bz;  // Controlled_Buffer controlled_buffer_97
  assign flag_h_out = rla ? not_7_out : 1'bz;  // Controlled_Buffer controlled_buffer_98
  assign flag_n_out = rla ? not_8_out : 1'bz;  // Controlled_Buffer controlled_buffer_99
  assign flag_c_out = rla ? controlled_buffer_73_out[7] : 1'bz;  // Controlled_Buffer controlled_buffer_100
  assign flag_z_out = rla ? flag_z_in : 1'bz;  // Controlled_Buffer controlled_buffer_101
  assign flag_pv_out = rla ? flag_pv_in : 1'bz;  // Controlled_Buffer controlled_buffer_102
  assign flag_s_out = rla ? flag_s_in : 1'bz;  // Controlled_Buffer controlled_buffer_103
  not not_11 (not_11_out, ccf);
  not not_12 (not_12_out, flag_c_in);
  assign acc_out = rlca ? {controlled_buffer_71_out[6:0], controlled_buffer_71_out[7]} : 8'bz;  // Controlled_Buffer controlled_buffer_104
  assign acc_out = rra ? {flag_c_in, controlled_buffer_72_out[7:1]} : 8'bz;  // Controlled_Buffer controlled_buffer_105
  assign flag_z_out = temp ? inc_8bit_1_flag_z : 1'bz;  // Controlled_Buffer controlled_buffer_106
  assign flag_h_out = temp ? inc_8bit_1_flag_h : 1'bz;  // Controlled_Buffer controlled_buffer_107
  assign flag_pv_out = temp ? inc_8bit_1_flag_pv : 1'bz;  // Controlled_Buffer controlled_buffer_108
  assign flag_n_out = temp ? inc_8bit_1_flag_n : 1'bz;  // Controlled_Buffer controlled_buffer_109
  assign flag_h_out = ccf ? flag_h_in : 1'bz;  // Controlled_Buffer controlled_buffer_110
  assign flag_n_out = ccf ? not_11_out : 1'bz;  // Controlled_Buffer controlled_buffer_111
  assign flag_c_out = ccf ? not_12_out : 1'bz;  // Controlled_Buffer controlled_buffer_112
  assign flag_z_out = ccf ? flag_z_in : 1'bz;  // Controlled_Buffer controlled_buffer_113
  assign flag_pv_out = ccf ? flag_pv_in : 1'bz;  // Controlled_Buffer controlled_buffer_114
  assign flag_s_out = ccf ? flag_s_in : 1'bz;  // Controlled_Buffer controlled_buffer_115
  assign acc_out = rla ? {controlled_buffer_73_out[6:0], flag_c_in} : 8'bz;  // Controlled_Buffer controlled_buffer_116
  assign acc_out = temp ? inc_8bit_1_inc_out : 8'bz;  // Controlled_Buffer controlled_buffer_117
  assign flag_s_out = temp ? inc_8bit_1_flag_s : 1'bz;  // Controlled_Buffer controlled_buffer_118
  nor nor_1 (nor_1_out, op_code[4], op_code[6], op_code[7]);
  and and_2 (and_2_out, op_code[0], op_code[1], op_code[2], op_code[3], op_code[4]);
  and and_3 (and_3_out, op_code[0], op_code[1], op_code[2], op_code[3]);
  and and_4 (and_4_out, op_code[0], op_code[1], op_code[2], op_code[4]);
  and and_5 (and_5_out, op_code[0], op_code[1], op_code[2]);
  and and_6 (and_6_out, op_code[0], op_code[1], op_code[2], op_code[4], op_code[5]);
  and and_7 (and_7_out, op_code[0], op_code[1], op_code[2], op_code[3], op_code[4], op_code[5]);
  and and_8 (and_8_out, op_code[0], op_code[1], op_code[2], op_code[3], op_code[5]);
  or or_2 (instr16, op_code[8], op_code[9], op_code[10], op_code[11], op_code[12], op_code[13], op_code[14], op_code[15]);
  nor nor_2 (nor_2_out, op_code[5], op_code[6], op_code[7]);
  nor nor_3 (nor_3_out, op_code[4], op_code[5], op_code[6], op_code[7]);
  nor nor_4 (nor_4_out, op_code[3], op_code[5], op_code[6], op_code[7]);
  nor nor_5 (nor_5_out, op_code[3], op_code[4], op_code[5], op_code[6], op_code[7]);
  nor nor_6 (nor_6_out, op_code[6], op_code[7], op_code[3]);
  nor nor_7 (nor_7_out, op_code[6], op_code[7]);
  and and_9 (cpl, and_8_out, instr8, nor_1_out);
  and and_10 (and_10_out, op_code[9], op_code[10], op_code[14], op_code[15]);
  nor nor_8 (nor_8_out, op_code[8], op_code[11], op_code[12], op_code[13]);
  and and_11 (and_11_out, op_code[3], op_code[7]);
  nor nor_9 (nor_9_out, op_code[4], op_code[5], op_code[6]);
  and and_12 (and_12_out, op_code[9], op_code[10], op_code[11], op_code[14], op_code[15]);
  nor nor_10 (nor_10_out, op_code[8], op_code[12], op_code[13]);
  and and_13 (and_13_out, op_code[8], op_code[10], op_code[11], op_code[13], op_code[14], op_code[15], op_code[2], op_code[6]);
  nor nor_11 (nor_11_out, op_code[9], op_code[12], op_code[0], op_code[1], op_code[3], op_code[4], op_code[5], op_code[7]);
  not not_13 (instr8, instr16);
  and and_14 (ccf, and_7_out, nor_7_out, instr8);
  nor nor_12 (nor_12_out, op_code[3], op_code[4], op_code[5], op_code[6]);
  and and_15 (and_15_out, and_10_out, nor_8_out);
  and and_16 (and_16_out, and_12_out, nor_10_out);
  and and_17 (rra, and_2_out, nor_2_out, instr8);
  and and_18 (rrca, and_3_out, nor_3_out, instr8);
  and and_19 (rla, and_4_out, nor_4_out, instr8);
  and and_20 (rlca, and_5_out, nor_5_out, instr8);
  and and_21 (scf, and_6_out, nor_6_out, instr8);
  and and_22 (and_22_out, nor_12_out, instr8, op_code[7]);
  and and_23 (and_23_out, and_11_out, instr8, nor_9_out);
  or or_3 (adc, and_23_out, and_16_out);
  and and_24 (neg, and_13_out, nor_11_out);
  or or_4 (add, and_22_out, and_15_out);
  and and_25 (and_25_out, op_code[3], op_code[4], op_code[7]);
  nor nor_13 (nor_13_out, op_code[5], op_code[6]);
  and and_26 (and_26_out, op_code[4], op_code[7]);
  nor nor_14 (nor_14_out, op_code[3], op_code[5], op_code[6]);
  nor nor_15 (nor_15_out, op_code[8], op_code[13]);
  and and_27 (and_27_out, op_code[9], op_code[10], op_code[11], op_code[12], op_code[14], op_code[15]);
  and and_28 (and_28_out, op_code[5], op_code[7]);
  nor nor_16 (nor_16_out, op_code[3], op_code[4], op_code[6]);
  nor nor_17 (nor_17_out, op_code[8], op_code[11], op_code[12]);
  and and_29 (and_29_out, op_code[9], op_code[10], op_code[13], op_code[14], op_code[15]);
  and and_30 (and_30_out, and_26_out, instr8, nor_14_out);
  and and_31 (and_31_out, op_code[9], op_code[10], op_code[12], op_code[14], op_code[15]);
  nand nand_1 (nand_1_out, op_code[8], op_code[11], op_code[13]);
  and and_32 (and_32_out, and_25_out, instr8, nor_13_out);
  and and_33 (and_33_out, nor_15_out, and_27_out);
  and and_34 (and_34_out, and_28_out, instr8, nor_16_out);
  and and_35 (and_35_out, nor_17_out, and_29_out);
  or or_5 (alu_operation, add, adc, temp, temp, ORl, XORl, sbc, ANDl, sub, cpl, neg, rlca, rla, rrca, rra);
  and and_36 (and_36_out, and_31_out, nand_1_out);
  or or_6 (sbc, and_32_out, and_33_out);
  or or_7 (sub, and_30_out, and_36_out);
  or or_8 (ANDl, and_34_out, and_35_out);
  nor nor_18 (nor_18_out, op_code[8], op_code[11]);
  and and_37 (and_37_out, op_code[9], op_code[10], op_code[12], op_code[13], op_code[14], op_code[15]);
  and and_38 (and_38_out, op_code[3], op_code[5], op_code[7]);
  nor nor_19 (nor_19_out, op_code[4], op_code[6]);
  nor nor_20 (nor_20_out, op_code[8], op_code[12]);
  and and_39 (and_39_out, op_code[9], op_code[10], op_code[11], op_code[13], op_code[14], op_code[15]);
  nor nor_21 (nor_21_out, op_code[3], op_code[6]);
  and and_40 (and_40_out, op_code[4], op_code[5], op_code[7]);
  and and_41 (and_41_out, nor_18_out, and_37_out);
  and and_42 (and_42_out, and_38_out, instr8, nor_19_out);
  and and_43 (and_43_out, nor_20_out, and_39_out);
  and and_44 (and_44_out, nor_21_out, instr8, and_40_out);
  assign flag_z_out = not_15_out ? flag_z_in : 1'bz;  // Controlled_Buffer controlled_buffer_119
  or or_9 (ORl, and_44_out, and_41_out);
  or or_10 (XORl, and_42_out, and_43_out);
  not not_14 (not_14_out, op_code[8]);
  and and_45 (and_45_out, op_code[9], op_code[10], op_code[11], op_code[12], op_code[13], op_code[14], op_code[15]);
  not not_15 (not_15_out, flags_operation);
  or or_11 (flags_operation, add, adc, temp, temp, ORl, XORl, cp, sbc, ANDl, sub, cpl, neg, ccf, scf, rlca, rla, rrca, rra);
  and and_46 (and_46_out, op_code[3], op_code[4], op_code[5], op_code[7]);
  not not_16 (not_16_out, op_code[6]);
  and and_47 (and_47_out, not_14_out, and_45_out);
  and and_48 (and_48_out, and_46_out, instr8, not_16_out);
  assign flag_pv_out = not_15_out ? flag_pv_in : 1'bz;  // Controlled_Buffer controlled_buffer_120
  assign flag_n_out = not_15_out ? flag_n_in : 1'bz;  // Controlled_Buffer controlled_buffer_121
  assign flag_s_out = not_15_out ? flag_s_in : 1'bz;  // Controlled_Buffer controlled_buffer_122
  or or_12 (cp, and_48_out, and_47_out);
  assign flag_c_out = not_15_out ? flag_c_in : 1'bz;  // Controlled_Buffer controlled_buffer_123
  assign flag_h_out = not_15_out ? flag_h_in : 1'bz;  // Controlled_Buffer controlled_buffer_124

  // Other names for the same wires on the sheet: flag_c = flag_c_out; flag_h = flag_h_out; flag_n = flag_n_out;
  //   flag_pv = flag_pv_out; flag_s = flag_s_out; flag_z = flag_z_out; dec = temp; inc = temp

  // Notes on the sheet:
  //   DODAC AND DO OPERACJI 8BIT
  //   temp
endmodule

module FLAG_REG (
  input  flag_C_in,
  input  flag_N_in,
  input  flag_PV_in,
  input  flag_H_in,
  input  flag_Z_in,
  input  flag_S_in,
  input  clock,
  input  alu_enable,
  output [7:0] out_9,
  output flag_C_out,
  output flag_N_out,
  output flag_PV_out,
  output flag_H_out,
  output flag_Z_out,
  output flag_S_out
);

  wire undriven_2;
  wire [5:3] undriven;

  Register register_1 (
    .D({flag_S_in, flag_Z_in, undriven[5], flag_H_in, undriven[3], flag_PV_in, flag_N_in, flag_C_in}),
    .en(undriven_2), .clk(clock),
    .Q({flag_S_out, flag_Z_out, out_9[5], flag_H_out, out_9[3], flag_PV_out, flag_N_out, flag_C_out}));  // open: clr

  assign {out_9[7:6], out_9[4], out_9[2:0]} = {flag_S_out, flag_Z_out, flag_H_out, flag_PV_out, flag_N_out, flag_C_out};
endmodule

module sub_8bit (
  input  [7:0] reg_A_in,
  input  [7:0] op_1,
  output [7:0] reg_a_out,
  output flag_z,
  output flag_s,
  output flag_h,
  output flag_c,
  output flag_pv,
  output flag_n
);

  wire subtractor_3_bout;

  Subtractor subtractor_1 (.a(reg_A_in), .b(op_1), .out({flag_s, reg_a_out[6:0]}), .bout(flag_c));  // open: bin
  Subtractor #(.width(4)) subtractor_2 (.a(op_1[3:0]), .b(reg_A_in[3:0]), .bout(flag_h));  // open: out, bin
  Subtractor #(.width(7)) subtractor_3 (.a(reg_A_in[6:0]), .b(op_1[6:0]), .bout(subtractor_3_bout));  // open: out, bin
  nor nor_1 (flag_z, reg_a_out[0], reg_a_out[1], reg_a_out[2], reg_a_out[3], reg_a_out[4], reg_a_out[5], reg_a_out[6], flag_s);
  xor xor_1 (flag_pv, flag_c, subtractor_3_bout);

  assign flag_n = 1'b1;
  assign reg_a_out[7] = flag_s;
endmodule

module sbc_8bit (
  input  flag_c_in,
  input  [7:0] acc_in,
  input  [7:0] reg_in,
  output [7:0] acc_out,
  output flag_c_out,
  output flag_z,
  output flag_s,
  output flag_n,
  output flag_pv,
  output flag_h
);

  Subtractor #(.width(4)) subtractor_1 (
    .a(acc_in[3:0]), .b(reg_in[3:0]), .out(acc_out[3:0]), .bin(flag_c_in), .bout(flag_h));
  Subtractor #(.width(4)) subtractor_2 (
    .a(acc_in[7:4]), .b(reg_in[7:4]), .out(acc_out[7:4]), .bin(flag_h), .bout(flag_c_out));
  nor nor_1 (flag_z, acc_out[0], acc_out[1], acc_out[2], acc_out[3], acc_out[4], acc_out[5], acc_out[6], acc_out[7]);
  not not_1 (flag_pv, 1'b1);

  assign flag_n = 1'b1;
  assign flag_s = acc_out[7];
endmodule

module adc_8bit (
  input  flag_c_in,
  input  [7:0] acc_in,
  input  [7:0] reg_in,
  output [7:0] acc_out,
  output flag_h,
  output flag_z,
  output flag_s,
  output flag_pv,
  output flag_n,
  output flag_c_out
);

  wire adder_2_cout;

  Adder #(.width(4)) adder_1 (.a(acc_in[3:0]), .b(reg_in[3:0]), .out(acc_out[3:0]), .cin(flag_c_in), .cout(flag_h));
  Adder #(.width(3)) adder_2 (.a(acc_in[6:4]), .b(reg_in[6:4]), .out(acc_out[6:4]), .cin(flag_h), .cout(adder_2_cout));
  Adder #(.width(1)) adder_3 (.a(reg_in[7]), .b(acc_in[7]), .out(acc_out[7]), .cin(adder_2_cout), .cout(flag_c_out));
  xor xor_1 (flag_pv, adder_2_cout, flag_c_out);
  nor nor_1 (flag_z, acc_out[0], acc_out[1], acc_out[2], acc_out[3], acc_out[4], acc_out[5], acc_out[6], acc_out[7]);
  not not_1 (flag_n, 1'b1);

  assign flag_s = acc_out[7];
endmodule

module cp_8bit (
  input  [7:0] reg_A_in,
  input  [7:0] op_1,
  output flag_z,
  output flag_s,
  output flag_h,
  output flag_c,
  output flag_pv,
  output flag_n
);

  wire subtractor_3_bout;
  wire [6:0] subtractor_1_out;

  Subtractor subtractor_1 (.a(reg_A_in), .b(op_1), .out({flag_s, subtractor_1_out}), .bout(flag_c));  // open: bin
  Subtractor #(.width(4)) subtractor_2 (.a(op_1[3:0]), .b(reg_A_in[3:0]), .bout(flag_h));  // open: out, bin
  Subtractor #(.width(7)) subtractor_3 (.a(reg_A_in[6:0]), .b(op_1[6:0]), .bout(subtractor_3_bout));  // open: out, bin
  nor nor_1 (flag_z, subtractor_1_out[0], subtractor_1_out[1], subtractor_1_out[2], subtractor_1_out[3], subtractor_1_out[4], subtractor_1_out[5], subtractor_1_out[6], flag_s);
  xor xor_1 (flag_pv, flag_c, subtractor_3_bout);

  assign flag_n = 1'b1;
endmodule

module neg_8bit (
  input  [7:0] acc_in,
  output [7:0] acc_out,
  output flag_z,
  output flag_c_out,
  output flag_s,
  output flag_h,
  output flag_n,
  output flag_pv
);

  wire nor_1_out;

  Subtractor #(.width(4)) subtractor_1 (.a(4'b0000), .b(acc_in[3:0]), .out(acc_out[3:0]), .bout(flag_h));  // open: bin
  Subtractor #(.width(4)) subtractor_2 (.a(4'b0000), .b(acc_in[7:4]), .out(acc_out[7:4]), .bin(flag_h));  // open: bout
  or or_1 (flag_c_out, acc_in[0], acc_in[1], acc_in[2], acc_in[3], acc_in[4], acc_in[5], acc_in[6], acc_in[7]);
  nor nor_1 (nor_1_out, acc_in[0], acc_in[1], acc_in[2], acc_in[3], acc_in[4], acc_in[5], acc_in[6]);
  and and_1 (flag_pv, nor_1_out, acc_in[7]);
  nor nor_2 (flag_z, acc_out[0], acc_out[1], acc_out[2], acc_out[3], acc_out[4], acc_out[5], acc_out[6], acc_out[7]);

  assign flag_n = 1'b1;
  assign flag_s = acc_out[7];
endmodule
