// Logisim project z80_add_8bit.circ as structural Verilog: 1 circuit, main circuit registers
module registers (
  input  [7:0] in_1,
  input  [7:0] in_2,
  input  [7:0] in_3,
  input  [7:0] in_4,
  input  [7:0] in_5,
  input  [2:0] in_6,
  input  [7:0] in_7,
  input  in_8
);

  wire adder_1_cout, clock_1_out;
  wire [7:0] adder_1_out, multiplexer_1_out, register_1_q, register_2_q, register_3_q, register_4_q,
       register_5_q, register_6_q, register_8_q;

  Clock clock_1 (.out(clock_1_out));
  Register register_1 (.D(in_1), .clk(clock_1_out), .Q(register_1_q));  // open: en, clr
  Register register_2 (.D(in_2), .clk(clock_1_out), .Q(register_2_q));  // open: en, clr
  Register register_3 (.D(in_3), .clk(clock_1_out), .Q(register_3_q));  // open: en, clr
  Register register_4 (.D(in_4), .clk(clock_1_out), .Q(register_4_q));  // open: en, clr
  Register register_5 (.D(in_5), .clk(clock_1_out), .Q(register_5_q));  // open: en, clr
  Register register_6 (.D(in_7), .clk(clock_1_out), .Q(register_6_q));  // open: en, clr
  Multiplexer #(.select(3), .width(8)) multiplexer_1 (
    .in0(register_1_q), .in1(register_2_q), .in2(register_3_q), .in3(register_4_q), .in4(register_5_q),
    .in5(register_6_q), .in7(register_8_q), .out(multiplexer_1_out), .sel(in_6));  // open: in6
  Adder adder_1 (.a(multiplexer_1_out), .b(register_8_q), .out(adder_1_out), .cout(adder_1_cout));  // open: cin
  Register #(.width(1)) register_7 (.D(adder_1_cout), .clk(clock_1_out), .clr(in_8));  // open: en, Q
  Register register_8 (.D(adder_1_out), .clk(clock_1_out), .Q(register_8_q), .clr(in_8));  // open: en
endmodule
