// Logisim project z80_sbc_8bit.circ as structural Verilog: 1 circuit, main circuit sbc
module sbc (
  input  [7:0] acc_in,
  input  [7:0] reg_in,
  output flag_h,
  output [7:0] acc_out,
  output flag_z,
  output flag_s,
  output flag_n,
  output flag_pv
);

  wire clk_out, flag_c_q, subtractor_2_bout;

  Clock clk (.out(clk_out));
  Subtractor #(.width(4)) subtractor_1 (
    .a(acc_in[3:0]), .b(reg_in[3:0]), .out(acc_out[3:0]), .bin(flag_c_q), .bout(flag_h));
  Subtractor #(.width(4)) subtractor_2 (
    .a(acc_in[7:4]), .b(reg_in[7:4]), .out(acc_out[7:4]), .bin(flag_h), .bout(subtractor_2_bout));
  Register #(.width(1)) flag_c (.D(subtractor_2_bout), .clk(clk_out), .Q(flag_c_q));  // open: en, clr
  nor nor_1 (flag_z, acc_out[0], acc_out[1], acc_out[2], acc_out[3], acc_out[4], acc_out[5], acc_out[6], acc_out[7]);
  not not_1 (flag_pv, 1'b1);

  assign flag_n = 1'b1;
  assign flag_s = acc_out[7];
endmodule
